# Fritzing sketch Blind Berlt Sketch (saved by Fritzing 0.9.3b)
breadboards: 1

parts:
  Part1 = Arduino Uno (Rev3)
  J1 = Piezo Speaker
  VCC1 = Battery block 9V  # not connected
  hc-sr1 = hc-sr04

nets:
  N1: Part1.D11_PWM/MOSI, J1.pin2
  N2: Part1.D12/MISO, hc-sr1.Echo
  N3: Part1.D13/SCK, hc-sr1.Trig
  5V: Part1.5V, hc-sr1.VCC
  GND: Part1.GND, J1.pin1, hc-sr1.GND
